// Logisim project SHYNAIYM_circuit.circ as structural Verilog: 4 circuits, main circuit main
module main (
  input  reset
);

  wire clock_1_out, comparator_1_eq, not_1_out, not_2_out;
  wire [6:0] keyboard_1_data;
  wire [7:0] ascii_1_out_2, controlled_buffer_1_out, controlled_buffer_3_out, inc_8_1_f, register_13_q,
       rom_1_data, t0, t1, t2, t3, t4, t5, t6, t7, t8, t9, t10, t11, t12, t13, t14, t15, t16, t17, t18, t19,
       t20, t21, t22, t23, t24, t25, t26, t27, t28, t29, t30, t31;

  Clock clock_1 (.out(clock_1_out));
  DotMatrix #(.matrixcols(32), .matrixrows(8)) dotmatrix_1 (
    .col0(t31), .col1(t30), .col2(t29), .col3(t28), .col4(t27), .col5(t26), .col6(t25), .col7(t24),
    .col8(t23), .col9(t22), .col10(t21), .col11(t20), .col12(t19), .col13(t18), .col14(t17), .col15(t16),
    .col16(t15), .col17(t14), .col18(t13), .col19(t12), .col20(t11), .col21(t10), .col22(t9), .col23(t8),
    .col24(t7), .col25(t6), .col26(t5), .col27(t4), .col28(t3), .col29(t2), .col30(t1), .col31(t0));
  Register register_1 (.D(t15), .Q(t16), .clk(clock_1_out), .clr(reset));  // open: en
  Register register_2 (.D(t14), .Q(t15), .clk(clock_1_out), .clr(reset));  // open: en
  Register register_3 (.D(t16), .Q(t17), .clk(clock_1_out), .clr(reset));  // open: en
  Register register_4 (.D(t13), .Q(t14), .clk(clock_1_out), .clr(reset));  // open: en
  Keyboard keyboard_1 (.clk(comparator_1_eq), .clr(reset), .data(keyboard_1_data));  // open: re, avail
  Register register_5 (.D(t17), .Q(t18), .clk(clock_1_out), .clr(reset));  // open: en
  Register register_6 (.D(t12), .Q(t13), .clk(clock_1_out), .clr(reset));  // open: en
  Register register_7 (.D(t18), .Q(t19), .clk(clock_1_out), .clr(reset));  // open: en
  Register register_8 (.D(t11), .Q(t12), .clk(clock_1_out), .clr(reset));  // open: en
  ASCII ascii_1 (.char_code(keyboard_1_data), .out_2(ascii_1_out_2));
  Register register_9 (.D(t19), .Q(t20), .clk(clock_1_out), .clr(reset));  // open: en
  Register register_10 (.D(t10), .Q(t11), .clk(clock_1_out), .clr(reset));  // open: en
  not not_1 (not_1_out, comparator_1_eq);
  assign controlled_buffer_1_out = comparator_1_eq ? ascii_1_out_2 : 8'bz;  // Controlled_Buffer controlled_buffer_1
  Register register_11 (.D(t20), .Q(t21), .clk(clock_1_out), .clr(reset));  // open: en
  Register register_12 (.D(t9), .Q(t10), .clk(clock_1_out), .clr(reset));  // open: en
  assign controlled_buffer_1_out = not_1_out ? inc_8_1_f : 8'bz;  // Controlled_Buffer controlled_buffer_2
  Register register_13 (.D(controlled_buffer_1_out), .Q(register_13_q), .clk(clock_1_out), .clr(reset));  // open: en
  Register register_14 (.D(t21), .Q(t22), .clk(clock_1_out), .clr(reset));  // open: en
  Register register_15 (.D(t22), .Q(t23), .clk(clock_1_out), .clr(reset));  // open: en
  Register register_16 (.D(t8), .Q(t9), .clk(clock_1_out), .clr(reset));  // open: en
  Register register_17 (.D(t7), .Q(t8), .clk(clock_1_out), .clr(reset));  // open: en
  Register register_18 (.D(t23), .Q(t24), .clk(clock_1_out), .clr(reset));  // open: en
  Register register_19 (.D(t6), .Q(t7), .clk(clock_1_out), .clr(reset));  // open: en
  Register register_20 (.D(t24), .Q(t25), .clk(clock_1_out), .clr(reset));  // open: en
  Register register_21 (.D(t5), .Q(t6), .clk(clock_1_out), .clr(reset));  // open: en
  Register register_22 (.D(t25), .Q(t26), .clk(clock_1_out), .clr(reset));  // open: en
  Register register_23 (.D(t4), .Q(t5), .clk(clock_1_out), .clr(reset));  // open: en
  ROM rom_1 (.addr(register_13_q), .data(rom_1_data));
  INC_8 inc_8_1 (.A(register_13_q), .CIN(1'b1), .F(inc_8_1_f));  // open: COUT
  Register register_24 (.D(t26), .Q(t27), .clk(clock_1_out), .clr(reset));  // open: en
  Register register_25 (.D(t3), .Q(t4), .clk(clock_1_out), .clr(reset));  // open: en
  Register register_26 (.D(t27), .Q(t28), .clk(clock_1_out), .clr(reset));  // open: en
  Register register_27 (.D(t2), .Q(t3), .clk(clock_1_out), .clr(reset));  // open: en
  Register register_28 (.D(t28), .Q(t29), .clk(clock_1_out), .clr(reset));  // open: en
  Register register_29 (.D(t1), .Q(t2), .clk(clock_1_out), .clr(reset));  // open: en
  Register register_30 (.D(t29), .Q(t30), .clk(clock_1_out), .clr(reset));  // open: en
  Register register_31 (.D(t30), .Q(t31), .clk(clock_1_out), .clr(reset));  // open: en
  Register register_32 (.D(t0), .Q(t1), .clk(clock_1_out), .clr(reset));  // open: en
  Register register_33 (.D(controlled_buffer_3_out), .Q(t0), .clk(clock_1_out), .clr(reset));  // open: en
  assign controlled_buffer_3_out = not_2_out ? rom_1_data : 8'bz;  // Controlled_Buffer controlled_buffer_3
  assign controlled_buffer_3_out = comparator_1_eq ? {8{1'b0}} : 8'bz;  // Controlled_Buffer controlled_buffer_4
  not not_2 (not_2_out, comparator_1_eq);
  Comparator #(.mode("unsigned")) comparator_1 (.a(rom_1_data), .b({8{1'b1}}), .eq(comparator_1_eq));  // open: gt, lt

  // Notes on the sheet:
  //   clock
  //   keyboard
  //   ledmatrix (display)
  //   t0-t31 tunnel
  //   ASCII
  //   address
  //   counter
  //   <READBOARD: SCROLL-IT>
  //   Built by: Amanaliyeva Shynaiym (24101212)
  //   It have: letters A-Z 
  //   Characters: exclamation mark, question mark, comma, period, space
  //   Click on Simulate>auto-tick enable (or Ctrl-K); select speed in Auto-tick frequency
  //   contents of rom_1 (hex, n*v repeats v):
  //   ff 7e 90 90 7e ff ff ff fe 92 92 6c 4*ff fe 82 82 82 4*ff fe 82 82 7c 4*ff fe 92 92 5*ff fe 90 90
  //   5*ff fe 82 92 9e 4*ff fe 10 10 fe 4*ff 82 fe 82 5*ff c 2 2 fc 4*ff fe 38 44 82 4*ff fe 2 2 5*ff fe
  //   60 38 60 fe ff ff ff fe 60 38 c fe ff ff ff fe 82 82 fe 4*ff fe 90 f0 5*ff fe 82 8a fe 4 ff ff ff fe
  //   98 94 62 4*ff f2 92 9e 4*ff f 80 fe 80 5*ff fe 2 fe 5*ff f8 6 f8 5*ff f8 6 78 6 f8 ff ff ff c6 28 10
  //   28 c6 ff ff ff f0 1e f0 5*ff 86 8a 92 a2 c2 ff ff ff 0 0 0 5*ff fa 7*ff 80 8a 90 60 4*ff 1 2 ff 2
  //   4*ff
endmodule

module INC_8 (
  input  [7:0] A,
  input  CIN,
  output COUT,
  output [7:0] F
);

  wire inc1_2_cout, inc1_3_cout, inc1_4_cout, inc1_5_cout, inc1_6_cout, inc1_7_cout, inc1_8_cout;

  INC1 inc1_1 (.CIN(inc1_2_cout), .A0(A[7]), .F0(F[7]), .COUT(COUT));
  INC1 inc1_2 (.CIN(inc1_3_cout), .A0(A[6]), .F0(F[6]), .COUT(inc1_2_cout));
  INC1 inc1_3 (.CIN(inc1_4_cout), .A0(A[5]), .F0(F[5]), .COUT(inc1_3_cout));
  INC1 inc1_4 (.CIN(inc1_5_cout), .A0(A[4]), .F0(F[4]), .COUT(inc1_4_cout));
  INC1 inc1_5 (.CIN(inc1_6_cout), .A0(A[3]), .F0(F[3]), .COUT(inc1_5_cout));
  INC1 inc1_6 (.CIN(inc1_7_cout), .A0(A[2]), .F0(F[2]), .COUT(inc1_6_cout));
  INC1 inc1_7 (.CIN(inc1_8_cout), .A0(A[1]), .F0(F[1]), .COUT(inc1_7_cout));
  INC1 inc1_8 (.CIN(CIN), .A0(A[0]), .F0(F[0]), .COUT(inc1_8_cout));
endmodule

module ASCII (
  input  [6:0] char_code,
  output [7:0] out_2
);

  wire comparator_1_eq, comparator_2_eq, comparator_3_eq, comparator_4_eq, comparator_5_eq, comparator_6_eq,
       comparator_7_eq, comparator_8_eq, comparator_9_eq, comparator_10_eq, comparator_11_eq,
       comparator_12_eq, comparator_13_eq, comparator_14_eq, comparator_15_eq, comparator_16_eq,
       comparator_17_eq, comparator_18_eq, comparator_19_eq, comparator_20_eq, comparator_21_eq,
       comparator_22_eq, comparator_23_eq, comparator_24_eq, comparator_25_eq, comparator_26_eq,
       comparator_27_eq, comparator_28_eq, comparator_29_eq, comparator_30_eq, comparator_31_eq,
       comparator_32_eq, comparator_33_eq, comparator_34_eq, comparator_35_eq, comparator_36_eq,
       comparator_37_eq, comparator_38_eq, comparator_39_eq, comparator_40_eq, comparator_41_eq,
       comparator_42_eq, comparator_43_eq, comparator_44_eq, comparator_45_eq;
  wire [7:0] bit_extender_1_out;

  assign bit_extender_1_out = {{1{1'b0}}, char_code};  // Bit_Extender bit_extender_1
  Comparator comparator_1 (.a(bit_extender_1_out), .b(8'h61), .eq(comparator_1_eq));  // open: gt, lt
  assign out_2 = comparator_1_eq ? 8'h1 : 8'bz;  // Controlled_Buffer controlled_buffer_1
  Comparator comparator_2 (.a(bit_extender_1_out), .b(8'h62), .eq(comparator_2_eq));  // open: gt, lt
  assign out_2 = comparator_2_eq ? 8'h8 : 8'bz;  // Controlled_Buffer controlled_buffer_2
  Comparator comparator_3 (.a(bit_extender_1_out), .b(8'h63), .eq(comparator_3_eq));  // open: gt, lt
  assign out_2 = comparator_3_eq ? 8'h10 : 8'bz;  // Controlled_Buffer controlled_buffer_3
  Comparator comparator_4 (.a(bit_extender_1_out), .b(8'h64), .eq(comparator_4_eq));  // open: gt, lt
  assign out_2 = comparator_4_eq ? 8'h18 : 8'bz;  // Controlled_Buffer controlled_buffer_4
  Comparator comparator_5 (.a(bit_extender_1_out), .b(8'h65), .eq(comparator_5_eq));  // open: gt, lt
  assign out_2 = comparator_5_eq ? 8'h20 : 8'bz;  // Controlled_Buffer controlled_buffer_5
  Comparator comparator_6 (.a(bit_extender_1_out), .b(8'h66), .eq(comparator_6_eq));  // open: gt, lt
  assign out_2 = comparator_6_eq ? 8'h28 : 8'bz;  // Controlled_Buffer controlled_buffer_6
  Comparator comparator_7 (.a(bit_extender_1_out), .b(8'h67), .eq(comparator_7_eq));  // open: gt, lt
  assign out_2 = comparator_7_eq ? 8'h30 : 8'bz;  // Controlled_Buffer controlled_buffer_7
  Comparator comparator_8 (.a(bit_extender_1_out), .b(8'h68), .eq(comparator_8_eq));  // open: gt, lt
  assign out_2 = comparator_8_eq ? 8'h38 : 8'bz;  // Controlled_Buffer controlled_buffer_8
  Comparator comparator_9 (.a(bit_extender_1_out), .b(8'h69), .eq(comparator_9_eq));  // open: gt, lt
  assign out_2 = comparator_9_eq ? 8'h40 : 8'bz;  // Controlled_Buffer controlled_buffer_9
  Comparator comparator_10 (.a(bit_extender_1_out), .b(8'h6a), .eq(comparator_10_eq));  // open: gt, lt
  assign out_2 = comparator_10_eq ? 8'h48 : 8'bz;  // Controlled_Buffer controlled_buffer_10
  Comparator comparator_11 (.a(bit_extender_1_out), .b(8'h6b), .eq(comparator_11_eq));  // open: gt, lt
  assign out_2 = comparator_11_eq ? 8'h50 : 8'bz;  // Controlled_Buffer controlled_buffer_11
  Comparator comparator_12 (.a(bit_extender_1_out), .b(8'h6c), .eq(comparator_12_eq));  // open: gt, lt
  assign out_2 = comparator_12_eq ? 8'h58 : 8'bz;  // Controlled_Buffer controlled_buffer_12
  Comparator comparator_13 (.a(bit_extender_1_out), .b(8'h6d), .eq(comparator_13_eq));  // open: gt, lt
  assign out_2 = comparator_13_eq ? 8'h60 : 8'bz;  // Controlled_Buffer controlled_buffer_13
  Comparator comparator_14 (.a(bit_extender_1_out), .b(8'h6e), .eq(comparator_14_eq));  // open: gt, lt
  assign out_2 = comparator_14_eq ? 8'h68 : 8'bz;  // Controlled_Buffer controlled_buffer_14
  Comparator comparator_15 (.a(bit_extender_1_out), .b(8'h6f), .eq(comparator_15_eq));  // open: gt, lt
  assign out_2 = comparator_15_eq ? 8'h70 : 8'bz;  // Controlled_Buffer controlled_buffer_15
  Comparator comparator_16 (.a(bit_extender_1_out), .b(8'h70), .eq(comparator_16_eq));  // open: gt, lt
  Comparator comparator_17 (.a(bit_extender_1_out), .b(8'h71), .eq(comparator_17_eq));  // open: gt, lt
  Comparator comparator_18 (.a(bit_extender_1_out), .b(8'h72), .eq(comparator_18_eq));  // open: gt, lt
  Comparator comparator_19 (.a(bit_extender_1_out), .b(8'h73), .eq(comparator_19_eq));  // open: gt, lt
  Comparator comparator_20 (.a(bit_extender_1_out), .b(8'h74), .eq(comparator_20_eq));  // open: gt, lt
  Comparator comparator_21 (.a(bit_extender_1_out), .b(8'h75), .eq(comparator_21_eq));  // open: gt, lt
  Comparator comparator_22 (.a(bit_extender_1_out), .b(8'h76), .eq(comparator_22_eq));  // open: gt, lt
  Comparator comparator_23 (.a(bit_extender_1_out), .b(8'h77), .eq(comparator_23_eq));  // open: gt, lt
  Comparator comparator_24 (.a(bit_extender_1_out), .b(8'h78), .eq(comparator_24_eq));  // open: gt, lt
  Comparator comparator_25 (.a(bit_extender_1_out), .b(8'h79), .eq(comparator_25_eq));  // open: gt, lt
  Comparator comparator_26 (.a(bit_extender_1_out), .b(8'h7a), .eq(comparator_26_eq));  // open: gt, lt
  Comparator comparator_27 (.a(bit_extender_1_out), .b(8'h20), .eq(comparator_27_eq));  // open: gt, lt
  Comparator comparator_28 (.a(bit_extender_1_out), .b(8'h21), .eq(comparator_28_eq));  // open: gt, lt
  Comparator comparator_29 (.a(bit_extender_1_out), .b(8'h3f), .eq(comparator_29_eq));  // open: gt, lt
  Comparator comparator_30 (.a(bit_extender_1_out), .b(8'h2c), .eq(comparator_30_eq));  // open: gt, lt
  assign out_2 = comparator_16_eq ? 8'h78 : 8'bz;  // Controlled_Buffer controlled_buffer_16
  assign out_2 = comparator_17_eq ? 8'h80 : 8'bz;  // Controlled_Buffer controlled_buffer_17
  assign out_2 = comparator_18_eq ? 8'h88 : 8'bz;  // Controlled_Buffer controlled_buffer_18
  assign out_2 = comparator_19_eq ? 8'h90 : 8'bz;  // Controlled_Buffer controlled_buffer_19
  assign out_2 = comparator_20_eq ? 8'h98 : 8'bz;  // Controlled_Buffer controlled_buffer_20
  assign out_2 = comparator_21_eq ? 8'ha0 : 8'bz;  // Controlled_Buffer controlled_buffer_21
  assign out_2 = comparator_22_eq ? 8'ha8 : 8'bz;  // Controlled_Buffer controlled_buffer_22
  assign out_2 = comparator_23_eq ? 8'hb0 : 8'bz;  // Controlled_Buffer controlled_buffer_23
  assign out_2 = comparator_24_eq ? 8'hb8 : 8'bz;  // Controlled_Buffer controlled_buffer_24
  assign out_2 = comparator_25_eq ? 8'hc0 : 8'bz;  // Controlled_Buffer controlled_buffer_25
  assign out_2 = comparator_26_eq ? 8'hc8 : 8'bz;  // Controlled_Buffer controlled_buffer_26
  assign out_2 = comparator_27_eq ? 8'hd0 : 8'bz;  // Controlled_Buffer controlled_buffer_27
  assign out_2 = comparator_28_eq ? 8'hd8 : 8'bz;  // Controlled_Buffer controlled_buffer_28
  assign out_2 = comparator_29_eq ? 8'he0 : 8'bz;  // Controlled_Buffer controlled_buffer_29
  assign out_2 = comparator_30_eq ? 8'he8 : 8'bz;  // Controlled_Buffer controlled_buffer_30
  Comparator comparator_31 (.a(bit_extender_1_out), .b(8'h31), .eq(comparator_31_eq));  // open: gt, lt
  Comparator comparator_32 (.a(bit_extender_1_out), .b(8'h32), .eq(comparator_32_eq));  // open: gt, lt
  Comparator comparator_33 (.a(bit_extender_1_out), .b(8'h33), .eq(comparator_33_eq));  // open: gt, lt
  Comparator comparator_34 (.a(bit_extender_1_out), .b(8'h34), .eq(comparator_34_eq));  // open: gt, lt
  Comparator comparator_35 (.a(bit_extender_1_out), .b(8'h35), .eq(comparator_35_eq));  // open: gt, lt
  Comparator comparator_36 (.a(bit_extender_1_out), .b(8'h36), .eq(comparator_36_eq));  // open: gt, lt
  Comparator comparator_37 (.a(bit_extender_1_out), .b(8'h37), .eq(comparator_37_eq));  // open: gt, lt
  Comparator comparator_38 (.a(bit_extender_1_out), .b(8'h38), .eq(comparator_38_eq));  // open: gt, lt
  Comparator comparator_39 (.a(bit_extender_1_out), .b(8'h39), .eq(comparator_39_eq));  // open: gt, lt
  Comparator comparator_40 (.a(bit_extender_1_out), .b(8'h30), .eq(comparator_40_eq));  // open: gt, lt
  Comparator comparator_41 (.a(bit_extender_1_out), .b(8'h2b), .eq(comparator_41_eq));  // open: gt, lt
  Comparator comparator_42 (.a(bit_extender_1_out), .b(8'h2d), .eq(comparator_42_eq));  // open: gt, lt
  Comparator comparator_43 (.a(bit_extender_1_out), .b(8'h2e), .eq(comparator_43_eq));  // open: gt, lt
  Comparator comparator_44 (.a(bit_extender_1_out), .b(8'h24), .eq(comparator_44_eq));  // open: gt, lt
  Comparator comparator_45 (.a(bit_extender_1_out), .b({8{1'b0}}), .eq(comparator_45_eq));  // open: gt, lt
  assign out_2 = comparator_31_eq ? 8'hf0 : 8'bz;  // Controlled_Buffer controlled_buffer_31
  assign out_2 = comparator_32_eq ? 8'hf8 : 8'bz;  // Controlled_Buffer controlled_buffer_32
  assign out_2 = comparator_33_eq ? {8{1'b0}} : 8'bz;  // Controlled_Buffer controlled_buffer_33
  assign out_2 = comparator_34_eq ? {8{1'b0}} : 8'bz;  // Controlled_Buffer controlled_buffer_34
  assign out_2 = comparator_35_eq ? {8{1'b0}} : 8'bz;  // Controlled_Buffer controlled_buffer_35
  assign out_2 = comparator_36_eq ? {8{1'b0}} : 8'bz;  // Controlled_Buffer controlled_buffer_36
  assign out_2 = comparator_37_eq ? {8{1'b0}} : 8'bz;  // Controlled_Buffer controlled_buffer_37
  assign out_2 = comparator_38_eq ? {8{1'b0}} : 8'bz;  // Controlled_Buffer controlled_buffer_38
  assign out_2 = comparator_39_eq ? {8{1'b0}} : 8'bz;  // Controlled_Buffer controlled_buffer_39
  assign out_2 = comparator_40_eq ? {8{1'b0}} : 8'bz;  // Controlled_Buffer controlled_buffer_40
  assign out_2 = comparator_41_eq ? {8{1'b0}} : 8'bz;  // Controlled_Buffer controlled_buffer_41
  assign out_2 = comparator_42_eq ? {8{1'b0}} : 8'bz;  // Controlled_Buffer controlled_buffer_42
  assign out_2 = comparator_43_eq ? {8{1'b0}} : 8'bz;  // Controlled_Buffer controlled_buffer_43
  assign out_2 = comparator_44_eq ? {8{1'b0}} : 8'bz;  // Controlled_Buffer controlled_buffer_44
  assign out_2 = comparator_45_eq ? {8{1'b0}} : 8'bz;  // Controlled_Buffer controlled_buffer_45

  // Notes on the sheet:
  //   char_code: initial=0x8
endmodule

module INC1 (
  input  CIN,
  input  A0,
  output F0,
  output COUT
);

  xor xor_1 (F0, CIN, A0);
  and and_1 (COUT, CIN, A0);
endmodule
